# Fritzing sketch prototype_schematic (saved by Fritzing 0.9.3b)
breadboards: 1

parts:
  Part1 = Arduino Uno (Rev3)
  J1 = Piezo Speaker
  LED1 = smd LED [color="Red (633nm)" package="0805 [SMD]"]
  R1 = Trimmer Potentiometer [maximum_resistance=10kΩ package=THT]
  S1 = Momentary Switch [package=tactile-pth]
  R2 = Resistor [tolerance=±5% resistance=220 package="0402 [SMD]"]
  R3 = Resistor [tolerance=±5% resistance=220 package="0402 [SMD]"]
  R4 = Resistor [tolerance=±5% resistance=220 package="0402 [SMD]"]
  R5 = Resistor [tolerance=±5% resistance=10k package="0402 [SMD]"]
  R6 = Resistor [tolerance=±5% resistance=10k package="0402 [SMD]"]
  LED2 = smd LED [color="Red (633nm)" package="0805 [SMD]"]
  LED3 = smd LED [color="Red (633nm)" package="0805 [SMD]"]

nets:
  N1: Part1.A0, R1.wiper
  N2: Part1.D9_PWM, J1.pin2
  N3: Part1.D2, S1.4, R6.Pin_1
  N4: Part1.D3_PWM, LED3.cathode
  N5: Part1.D4, LED2.cathode
  N6: Part1.D5_PWM, LED1.cathode
  N7: Part1.5V, R1.leg1, S1.3
  N8: Part1.GND, J1.pin1, R2.Pin_0, R3.Pin_0, R4.Pin_0, R5.Pin_0, R6.Pin_0
  N9: LED1.anode, R2.Pin_1
  N10: R1.leg2, R5.Pin_1
  N11: R3.Pin_1, LED2.anode
  N12: R4.Pin_1, LED3.anode

// code stored in the sketch: prototype_schematic.ino

